// Logisim project Assignment1_Q1.circ as structural Verilog: 1 circuit, main circuit main
module main (
  input  G3_msb,
  input  G2,
  input  G1,
  input  G0_lsb,
  output B3_msb,
  output B2,
  output B1,
  output B0_lsb
);

  wire and_1_out, and_2_out, and_3_out, and_4_out, and_5_out, and_6_out, not_1_out, not_2_out, not_3_out,
       not_4_out, not_5_out, not_6_out;

  not not_1 (not_1_out, G3_msb);
  not not_2 (not_2_out, G2);
  and and_1 (and_1_out, not_1_out, G2);
  and and_2 (and_2_out, not_2_out, G3_msb);
  or or_1 (B2, and_1_out, and_2_out);
  not not_3 (not_3_out, B2);
  not not_4 (not_4_out, G1);
  and and_3 (and_3_out, not_3_out, G1);
  and and_4 (and_4_out, B2, not_4_out);
  or or_2 (B1, and_3_out, and_4_out);
  not not_5 (not_5_out, B1);
  not not_6 (not_6_out, G0_lsb);
  and and_5 (and_5_out, not_5_out, G0_lsb);
  and and_6 (and_6_out, B1, not_6_out);
  or or_3 (B0_lsb, and_5_out, and_6_out);

  assign B3_msb = G3_msb;
endmodule
