// Logisim project Assignment1_Q2.circ as structural Verilog: 1 circuit, main circuit main
module main (
  input  G3_msb,
  input  G2,
  input  G1,
  input  G0_lsb,
  output B3_msb,
  output B2,
  output B1,
  output B0_lsb
);

  xor xor_1 (B2, G3_msb, G2);
  xor xor_2 (B1, B2, G1);
  xor xor_3 (B0_lsb, B1, G0_lsb);

  assign B3_msb = G3_msb;
endmodule
