// Logisim project Assignment_mux.circ as structural Verilog: 3 circuits, main circuit main
module main (
  input  En,
  input  S1,
  input  S2,
  input  I0,
  input  I1,
  input  I2,
  input  I3,
  output out_8
);

  wire and_1_out, and_2_out, and_3_out, and_4_out, not_1_out, not_2_out;

  not not_1 (not_1_out, S1);
  not not_2 (not_2_out, S2);
  and and_1 (and_1_out, not_1_out, not_2_out, I0, En);
  and and_2 (and_2_out, not_1_out, S2, I1, En);
  and and_3 (and_3_out, S1, not_2_out, I2, En);
  and and_4 (and_4_out, S1, S2, I3, En);
  or or_1 (out_8, and_1_out, and_2_out, and_3_out, and_4_out);

  // Notes on the sheet:
  //   4:1 Mux
endmodule

module _8_1 (
  input  En,
  input  S1,
  input  S0,
  input  I0,
  input  I1,
  input  I2,
  input  I3,
  input  I4,
  input  I5,
  input  I6,
  input  I7,
  output out_12
);

  wire main_1_out_8, main_2_out_8, not_1_out;

  not not_1 (not_1_out, En);
  main main_1 (.S1(S1), .S2(S0), .I0(I0), .I1(I1), .I2(I2), .I3(I3), .En(not_1_out), .out_8(main_1_out_8));
  main main_2 (.S1(S1), .S2(S0), .I0(I4), .I1(I5), .I2(I6), .I3(I7), .En(En), .out_8(main_2_out_8));
  or or_1 (out_12, main_1_out_8, main_2_out_8);
endmodule

module fnwith8_1 (
  input  A,
  input  B,
  input  C,
  input  D,
  input  in_5,
  output o_p
);

  wire not_1_out, not_2_out;

  not not_1 (not_1_out, D);
  not not_2 (not_2_out, in_5);
  _8_1 u_8_1_1 (
    .En(A), .S1(B), .S0(C), .I0(not_1_out), .I1(in_5), .I2(in_5), .I3(not_2_out), .I4(in_5), .I5(in_5),
    .I6(in_5), .I7(D), .out_12(o_p));

  // Notes on the sheet:
  //   8:1 Mux
endmodule
