// Logisim project Assignmnent7.circ as structural Verilog: 1 circuit, main circuit main
module main (
  input  A3,
  input  B3,
  input  A2,
  input  B2,
  input  A1,
  input  B1,
  input  A0,
  input  B0,
  output out_9,
  output Z_A_B,
  output Y_B_A
);

  wire and_1_out, and_2_out, and_3_out, and_4_out, and_5_out, and_6_out, and_7_out, and_8_out, not_1_out,
       not_2_out, not_3_out, not_4_out, not_5_out, not_6_out, not_7_out, not_8_out, xnor_1_out, xnor_2_out,
       xnor_3_out, xnor_4_out;

  not not_1 (not_1_out, B3);
  not not_2 (not_2_out, A3);
  not not_3 (not_3_out, A2);
  xnor xnor_1 (xnor_1_out, A2, B2);
  xnor xnor_2 (xnor_2_out, A1, B1);
  not not_4 (not_4_out, A1);
  not not_5 (not_5_out, B2);
  not not_6 (not_6_out, B1);
  xnor xnor_3 (xnor_3_out, A3, B3);
  not not_7 (not_7_out, A0);
  and and_1 (and_1_out, A3, not_1_out);
  and and_2 (and_2_out, A2, not_5_out);
  not not_8 (not_8_out, B0);
  and and_3 (and_3_out, A1, not_6_out);
  and and_4 (and_4_out, A0, not_8_out);
  xnor xnor_4 (xnor_4_out, A0, B0);
  and and_5 (and_5_out, not_2_out, B3);
  and and_6 (and_6_out, not_3_out, B2);
  and and_7 (and_7_out, not_4_out, B1);
  and and_8 (and_8_out, not_7_out, B0);
  and and_9 (Z_A_B, xnor_3_out, xnor_1_out, xnor_2_out, xnor_4_out);
  or or_1 (out_9, and_1_out, and_2_out, and_3_out, and_4_out);
  or or_2 (Y_B_A, and_5_out, and_6_out, and_7_out, and_8_out);

  // Notes on the sheet:
  //                    X(A>B)
endmodule
