// Logisim project DECODERS.circ as structural Verilog: 5 circuits, main circuit main
module main (
  input  EN,
  input  A0,
  output B1,
  output B0
);

  nand nand_1 (B1, EN, A0);
  not not_1 (B0, B1);
endmodule

module _1_2_bit_decoder (
  input  EN,
  input  A0,
  input  A1,
  input  A2,
  output P0,
  output P1,
  output P2,
  output P3,
  output P4,
  output P5,
  output P6,
  output P7
);

  wire not_1_out, not_2_out, not_3_out;

  not not_1 (not_1_out, A0);
  not not_2 (not_2_out, A1);
  not not_3 (not_3_out, A2);
  nand nand_1 (P0, EN, not_1_out, not_2_out, not_3_out);
  nand nand_2 (P1, EN, A0, not_2_out, not_3_out);
  nand nand_3 (P2, EN, not_1_out, A1, not_3_out);
  nand nand_4 (P3, EN, A0, A1, not_3_out);
  nand nand_5 (P4, EN, not_1_out, not_2_out, A2);
  nand nand_6 (P5, EN, A0, not_2_out, A2);
  nand nand_7 (P6, EN, not_1_out, A1, A2);
  nand nand_8 (P7, EN, A0, A1, A2);

  // Notes on the sheet:
  //   LSB
  //   MSB
  //   Thus no low value(0) is seen for A=0
  //   A is enable in the truth table
endmodule

module _3_to_8_decoder (
  input  in_1,
  input  X2,
  input  MSB,
  input  X1,
  input  X0,
  output A0,
  output A1,
  output A2,
  output A3,
  output A4,
  output A5,
  output A6,
  output A7,
  output A8,
  output A9,
  output A11,
  output A10,
  output A12,
  output A13,
  output A14,
  output MSB_2
);

  wire main_1_b0, main_1_b1;

  main main_1 (.EN(in_1), .A0(MSB), .B1(main_1_b1), .B0(main_1_b0));
  _1_2_bit_decoder u_1_2_bit_decoder_1 (
    .A0(X2), .A1(X1), .A2(X0), .EN(main_1_b1), .P0(A0), .P1(A1), .P2(A2), .P3(A3), .P4(A4), .P5(A5), .P6(A6),
    .P7(A7));
  _1_2_bit_decoder u_1_2_bit_decoder_2 (
    .A0(X2), .A1(X1), .A2(X0), .EN(main_1_b0), .P0(A8), .P1(A9), .P2(A11), .P3(A10), .P4(A12), .P5(A13),
    .P6(A14), .P7(MSB_2));

  // Notes on the sheet:
  //   LSB
  //   X3
  //   LSB
  //   A15
endmodule

module _4_16 (
  input  EN,
  input  A0,
  input  A1,
  input  A2,
  input  A3,
  output B0,
  output B1,
  output B2,
  output B3
);

  wire n3_to_8_decoder_1_a0, n3_to_8_decoder_1_a1, n3_to_8_decoder_1_a2, n3_to_8_decoder_1_a3,
       n3_to_8_decoder_1_a4, n3_to_8_decoder_1_a5, n3_to_8_decoder_1_a6, n3_to_8_decoder_1_a7,
       n3_to_8_decoder_1_a8, n3_to_8_decoder_1_a9;

  _3_to_8_decoder u_3_to_8_decoder_1 (
    .X2(A0), .MSB(A1), .X1(A2), .X0(A3), .in_1(EN), .A0(n3_to_8_decoder_1_a0), .A1(n3_to_8_decoder_1_a1),
    .A2(n3_to_8_decoder_1_a2), .A3(n3_to_8_decoder_1_a3), .A4(n3_to_8_decoder_1_a4),
    .A5(n3_to_8_decoder_1_a5), .A6(n3_to_8_decoder_1_a6), .A7(n3_to_8_decoder_1_a7),
    .A8(n3_to_8_decoder_1_a8), .A9(n3_to_8_decoder_1_a9));  // open: A11, A10, A12, A13, A14, MSB_2
  nand nand_1 (B0, n3_to_8_decoder_1_a6, n3_to_8_decoder_1_a7, n3_to_8_decoder_1_a8, n3_to_8_decoder_1_a9, n3_to_8_decoder_1_a0);
  nand nand_2 (B1, n3_to_8_decoder_1_a1, n3_to_8_decoder_1_a3, n3_to_8_decoder_1_a7, n3_to_8_decoder_1_a9);
  nand nand_3 (B2, n3_to_8_decoder_1_a1, n3_to_8_decoder_1_a4, n3_to_8_decoder_1_a5, n3_to_8_decoder_1_a8, n3_to_8_decoder_1_a9);
  nand nand_4 (B3, n3_to_8_decoder_1_a2, n3_to_8_decoder_1_a3, n3_to_8_decoder_1_a4, n3_to_8_decoder_1_a5, n3_to_8_decoder_1_a0);

  // Notes on the sheet:
  //   MSB
  //   INPUT:9(1001)
  //   LSB
  //   ID:2019A3PS1119P
  //   LSB
  //   MSB
endmodule

module BCD_to_Excess_3 (
  input  in_1,
  input  in_2,
  input  in_3,
  input  in_4,
  input  in_5,
  output out_6,
  output out_7,
  output out_8,
  output out_9
);

  _4_16 u_4_16_1 (
    .A0(in_2), .A1(in_3), .A2(in_4), .A3(in_5), .EN(in_1), .B0(out_6), .B1(out_7), .B2(out_9), .B3(out_8));
endmodule
