// Logisim project Half_adder.circ as structural Verilog: 5 circuits, main circuit main
module main (
  input  in_1,
  input  in_2,
  output out_3,
  output out_4
);

  xor xor_1 (out_3, in_1, in_2);
  and and_1 (out_4, in_1, in_2);
endmodule

module Half_Adder (
  input  in_1,
  input  in_2,
  input  in_3,
  output out_4,
  output out_5
);

  wire main_1_out_3, main_1_out_4, main_2_out_4;

  main main_1 (.in_1(in_1), .in_2(in_2), .out_3(main_1_out_3), .out_4(main_1_out_4));
  main main_2 (.in_1(main_1_out_3), .in_2(in_3), .out_3(out_4), .out_4(main_2_out_4));
  or or_1 (out_5, main_2_out_4, main_1_out_4);
endmodule

module BCD_Adder (
  input  in_1,
  input  in_2,
  input  in_3,
  input  in_4,
  input  in_5,
  input  in_6,
  input  in_7,
  input  in_8,
  input  in_9,
  input  in_10,
  input  in_11,
  output out_12,
  output out_13,
  output out_14,
  output out_15,
  output out_16,
  output out_17
);

  wire and_1_out, and_2_out, full_adder_1_cout, full_adder_1_s0, full_adder_1_s1, full_adder_1_s2,
       full_adder_1_s3;

  Full_Adder full_adder_1 (
    .Control(in_1), .A0(in_2), .B0(in_3), .A1(in_4), .B1(in_6), .A2(in_7), .B2(in_8), .A3(in_10), .B3(in_11),
    .S0(full_adder_1_s0), .S1(full_adder_1_s1), .S2(full_adder_1_s2), .S3(full_adder_1_s3),
    .Cout(full_adder_1_cout));
  and and_1 (and_1_out, full_adder_1_s0, full_adder_1_s1);
  and and_2 (and_2_out, full_adder_1_s0, full_adder_1_s2);
  or or_1 (out_12, full_adder_1_cout, and_1_out, and_2_out);
  Full_Adder full_adder_2 (
    .Control(out_13), .A0(full_adder_1_s0), .B0(in_5), .A1(full_adder_1_s1), .B1(out_12),
    .A2(full_adder_1_s2), .B2(out_12), .A3(full_adder_1_s3), .B3(in_9), .S0(out_14), .S1(out_15),
    .S2(out_16), .S3(out_17));  // open: Cout
endmodule

module Full_Adder (
  input  Control,
  input  A0,
  input  B0,
  input  A1,
  input  B1,
  input  A2,
  input  B2,
  input  A3,
  input  B3,
  output S0,
  output S1,
  output S2,
  output S3,
  output Cout
);

  wire half_adder_1_out_5, half_adder_2_out_5, half_adder_3_out_5, xor_1_out, xor_2_out, xor_3_out,
       xor_4_out, xor_5_out;

  xor xor_1 (xor_1_out, Control, B0);
  Half_Adder half_adder_1 (.in_1(Control), .in_2(A0), .in_3(xor_1_out), .out_4(S0), .out_5(half_adder_1_out_5));
  xor xor_2 (xor_2_out, Control, B1);
  xor xor_3 (xor_3_out, Control, B2);
  xor xor_4 (xor_4_out, Control, B3);
  Half_Adder half_adder_2 (
    .in_1(half_adder_1_out_5), .in_2(A1), .in_3(xor_2_out), .out_4(S1), .out_5(half_adder_2_out_5));
  Half_Adder half_adder_3 (
    .in_1(half_adder_2_out_5), .in_2(A2), .in_3(xor_3_out), .out_4(S2), .out_5(half_adder_3_out_5));
  Half_Adder half_adder_4 (.in_1(half_adder_3_out_5), .in_2(A3), .in_3(xor_4_out), .out_4(S3), .out_5(Cout));
  xor xor_5 (xor_5_out, half_adder_3_out_5, Cout);
  LED led_1 (.in(xor_5_out));

  // Notes on the sheet:
  //   A:2
  //   B:9
  //   ID:2019A3PS1119P
endmodule

module BCD_to_7seg (
  input  S1,
  input  S2,
  input  S3,
  input  S4,
  output A,
  output B,
  output C,
  output D,
  output E,
  output F,
  output G
);

  wire and_1_out, and_2_out, and_3_out, and_4_out, and_5_out, and_6_out, and_7_out, and_8_out, and_9_out,
       and_10_out, and_11_out, and_12_out, and_13_out, and_14_out, and_15_out, and_16_out, not_1_out,
       not_2_out, not_3_out, not_4_out, not_5_out, not_6_out, not_7_out, not_8_out, not_9_out, not_10_out,
       not_11_out, not_12_out, not_13_out, not_14_out, not_15_out, not_16_out, not_17_out, not_18_out,
       not_19_out, not_20_out, not_21_out;

  not not_1 (not_1_out, S2);
  and and_1 (and_1_out, not_1_out, not_2_out);
  not not_2 (not_2_out, S4);
  and and_2 (and_2_out, S2, S4);
  not not_3 (not_3_out, S2);
  not not_4 (not_4_out, S3);
  and and_3 (and_3_out, not_4_out, not_5_out);
  not not_5 (not_5_out, S4);
  and and_4 (and_4_out, S3, S4);
  not not_6 (not_6_out, S3);
  or or_1 (C, not_6_out, S4, S2);
  not not_7 (not_7_out, S2);
  and and_5 (and_5_out, not_7_out, not_8_out);
  not not_8 (not_8_out, S4);
  not not_9 (not_9_out, S2);
  and and_6 (and_6_out, not_9_out, S3);
  and and_7 (and_7_out, S3, not_10_out);
  not not_10 (not_10_out, S4);
  not not_11 (not_11_out, S3);
  and and_8 (and_8_out, S2, not_11_out, S4);
  not not_12 (not_12_out, S2);
  and and_9 (and_9_out, not_12_out, not_13_out);
  not not_13 (not_13_out, S4);
  and and_10 (and_10_out, S3, not_14_out);
  not not_14 (not_14_out, S4);
  not not_15 (not_15_out, S3);
  and and_11 (and_11_out, not_15_out, not_16_out);
  not not_16 (not_16_out, S4);
  and and_12 (and_12_out, S2, not_17_out);
  not not_17 (not_17_out, S3);
  and and_13 (and_13_out, S2, not_18_out);
  not not_18 (not_18_out, S4);
  not not_19 (not_19_out, S2);
  and and_14 (and_14_out, not_19_out, S3);
  and and_15 (and_15_out, S2, not_20_out);
  not not_20 (not_20_out, S3);
  and and_16 (and_16_out, S2, not_21_out);
  not not_21 (not_21_out, S4);
  or or_2 (A, and_1_out, S3, and_2_out, S1);
  or or_3 (B, not_3_out, and_3_out, and_4_out);
  or or_4 (D, and_5_out, and_6_out, and_7_out, and_8_out, S1);
  or or_5 (E, and_9_out, and_10_out);
  or or_6 (F, and_11_out, and_12_out, and_13_out, S1);
  or or_7 (G, and_14_out, and_15_out, and_16_out, S1);
endmodule
