// Logisim project Test.circ as structural Verilog: 1 circuit, main circuit main
module main (
  input  in_1,
  input  in_2,
  input  in_3
);

  wire and_1_out, not_1_out, or_1_out;

  or or_1 (or_1_out, in_1, in_2);
  not not_1 (not_1_out, in_3);
  and and_1 (and_1_out, or_1_out, not_1_out);
  _7_Segment_Display u_7_segment_display_1 (.f(and_1_out), .a(and_1_out), .d(and_1_out));  // open: g, b, e, c, dp
endmodule
