// Logisim project ass3_basicckts.circ as structural Verilog
module main (
  input  Pr,
  input  J,
  input  Ed,
  input  K,
  input  Cr,
  output out_6,
  output out_7
);

  wire nand_1_out, nand_2_out, nand_3_out, nand_4_out, nand_5_out, nand_6_out, not_1_out;

  nand nand_1 (nand_1_out, out_7, J, Ed);
  nand nand_2 (nand_2_out, Ed, K, out_6);
  not not_1 (not_1_out, Ed);
  nand nand_3 (nand_3_out, Pr, nand_1_out, nand_4_out);
  nand nand_4 (nand_4_out, nand_3_out, nand_2_out, Cr);
  nand nand_5 (nand_5_out, nand_3_out, not_1_out);
  nand nand_6 (nand_6_out, not_1_out, nand_4_out);
  nand nand_7 (out_6, Pr, nand_5_out, out_7);
  nand nand_8 (out_7, out_6, nand_6_out, Cr);

  // Notes on the sheet:
  //   MASTER
  //   SLAVE
endmodule

module JKms (
  input  P,
  input  T,
  input  C,
  input  in_4,
  output Q,
  output Q_prime
);

  main main_1 (.J(T), .Ed(in_4), .K(T), .Pr(P), .Cr(C), .out_6(Q), .out_7(Q_prime));
endmodule
