// Logisim project async mod 10 bin adder.circ as structural Verilog: 1 circuit, main circuit main
module main (
  input  in_1,
  output out_2,
  output out_3,
  output MSB,
  output LSB
);

  wire and_1_out, clock_1_out, j_k_ff_1_qn, j_k_ff_2_qn, j_k_ff_3_qn;

  Clock clock_1 (.out(clock_1_out));
  J_K_Flip_Flop j_k_ff_1 (
    .J(in_1), .clk(clock_1_out), .K(in_1), .Q(LSB), .Qn(j_k_ff_1_qn), .reset(and_1_out));  // open: preset, en
  and and_1 (and_1_out, out_2, j_k_ff_3_qn, j_k_ff_1_qn, MSB);
  J_K_Flip_Flop j_k_ff_2 (
    .J(in_1), .clk(j_k_ff_1_qn), .K(in_1), .Q(out_2), .Qn(j_k_ff_2_qn), .reset(and_1_out));  // open: preset, en
  J_K_Flip_Flop j_k_ff_3 (
    .J(in_1), .clk(j_k_ff_2_qn), .K(in_1), .Q(out_3), .Qn(j_k_ff_3_qn), .reset(and_1_out));  // open: preset, en
  J_K_Flip_Flop j_k_ff_4 (.J(in_1), .clk(j_k_ff_3_qn), .K(in_1), .Q(MSB), .reset(and_1_out));  // open: Qn, preset, en
endmodule
