// Logisim project sequence detector(1001).circ as structural Verilog: 1 circuit, main circuit main
module main (
  input  X,
  output Z
);

  wire and_1_out, and_2_out, clock_1_out, d_ff_1_q, d_ff_2_q, not_1_out, not_2_out, or_1_out, xor_1_out;

  not not_1 (not_1_out, d_ff_2_q);
  not not_2 (not_2_out, X);
  xor xor_1 (xor_1_out, d_ff_1_q, d_ff_2_q);
  and and_1 (and_1_out, d_ff_1_q, not_1_out);
  and and_2 (and_2_out, not_2_out, xor_1_out);
  or or_1 (or_1_out, and_1_out, X);
  Clock clock_1 (.out(clock_1_out));
  D_Flip_Flop d_ff_1 (.clk(clock_1_out), .D(and_2_out), .Q(d_ff_1_q));  // open: Qn, preset, en, reset
  D_Flip_Flop d_ff_2 (.clk(clock_1_out), .D(or_1_out), .Q(d_ff_2_q));  // open: Qn, preset, en, reset
  and and_3 (Z, X, d_ff_1_q, d_ff_2_q);

  // Notes on the sheet:
  //   CLK
  //   2019A3PS1119P
endmodule
